// Digital circuit 8-bit-memory.dig as structural Verilog
module _8_bit_memory (
  input  Input_0,
  input  Input_1,
  input  Input_2,
  input  Input_3,
  input  Input_4,
  input  Input_5,
  input  Input_6,
  input  Input_7,
  input  Read_Write,
  input  Operate,
  output Output_0,
  output Output_1,
  output Output_2,
  output Output_3,
  output Output_4,
  output Output_5,
  output Output_6,
  output Output_7
);

  _1_bit_memory _1_bit_memory_1 (
    .InputBit(Input_7), .Read_WriteMode(Read_Write), .OutputBit(Output_7), .Enable(Operate));
  _1_bit_memory _1_bit_memory_2 (
    .InputBit(Input_6), .Read_WriteMode(Read_Write), .OutputBit(Output_6), .Enable(Operate));
  _1_bit_memory _1_bit_memory_3 (
    .InputBit(Input_5), .Read_WriteMode(Read_Write), .OutputBit(Output_5), .Enable(Operate));
  _1_bit_memory _1_bit_memory_4 (
    .InputBit(Input_4), .Read_WriteMode(Read_Write), .OutputBit(Output_4), .Enable(Operate));
  _1_bit_memory _1_bit_memory_5 (
    .InputBit(Input_3), .Read_WriteMode(Read_Write), .OutputBit(Output_3), .Enable(Operate));
  _1_bit_memory _1_bit_memory_6 (
    .InputBit(Input_2), .Read_WriteMode(Read_Write), .OutputBit(Output_2), .Enable(Operate));
  _1_bit_memory _1_bit_memory_7 (
    .InputBit(Input_1), .Read_WriteMode(Read_Write), .OutputBit(Output_1), .Enable(Operate));
  _1_bit_memory _1_bit_memory_8 (
    .InputBit(Input_0), .Read_WriteMode(Read_Write), .OutputBit(Output_0), .Enable(Operate));
endmodule
