// Digital circuit all-instructions.dig as structural Verilog
module all_instructions (
  input  Store1_i_0,
  input  Store1_m_0,
  input  Store1_m_1,
  input  Store1_m_2,
  input  Store1_r_w,
  input  Load1_m_0,
  input  Store1_i_1,
  input  Store1_i_2,
  input  Store1_i_3,
  input  Store1_i_4,
  input  Store1_i_5,
  input  Store1_i_6,
  input  Store1_i_7,
  input  Store2_m_0,
  input  Store2_r_w,
  input  Store2_m_1,
  input  Store2_m_2,
  input  Store2_i_0,
  input  Store2_i_1,
  input  Store2_i_2,
  input  Store2_i_3,
  input  Store2_i_4,
  input  Store2_i_5,
  input  Store2_i_6,
  input  Store2_i_7,
  input  Load1_m_1,
  input  Load1_m_2,
  input  Load2_m_0,
  input  Load2_m_1,
  input  Load2_m_2,
  input  Substraction,
  input  Store3_m_0,
  input  Store3_r_w,
  input  Store3_m_1,
  input  Store3_m_2,
  input  On_Off,
  input  Clk
);

  wire _8_bit_memories_1_done, _8_bit_memories_1_output_0, _8_bit_memories_1_output_1,
       _8_bit_memories_1_output_2, _8_bit_memories_1_output_3, _8_bit_memories_1_output_4,
       _8_bit_memories_1_output_5, _8_bit_memories_1_output_6, _8_bit_memories_1_output_7,
       _8_bit_memories_2_done, _8_bit_memories_2_output_0, _8_bit_memories_2_output_1,
       _8_bit_memories_2_output_2, _8_bit_memories_2_output_3, _8_bit_memories_2_output_4,
       _8_bit_memories_2_output_5, _8_bit_memories_2_output_6, _8_bit_memories_2_output_7,
       _8_bit_memories_3_done, _8_bit_memories_3_output_0, _8_bit_memories_3_output_1,
       _8_bit_memories_3_output_2, _8_bit_memories_3_output_3, _8_bit_memories_3_output_4,
       _8_bit_memories_3_output_5, _8_bit_memories_3_output_6, _8_bit_memories_3_output_7,
       _8_bit_register_1_o_0, _8_bit_register_1_o_1, _8_bit_register_1_o_2, _8_bit_register_1_o_3,
       _8_bit_register_1_o_4, _8_bit_register_1_o_5, _8_bit_register_1_o_6, _8_bit_register_1_o_7,
       _8_bit_register_2_o_0, _8_bit_register_2_o_1, _8_bit_register_2_o_2, _8_bit_register_2_o_3,
       _8_bit_register_2_o_4, _8_bit_register_2_o_5, _8_bit_register_2_o_6, _8_bit_register_2_o_7,
       alu_1_done, alu_1_o_bit_0, alu_1_o_bit_1, alu_1_o_bit_2, alu_1_o_bit_3, alu_1_o_bit_4, alu_1_o_bit_5,
       alu_1_o_bit_6, alu_1_o_bit_7, and_1_out, and_2_out, and_3_out, d_ff_1_q, d_ff_2_q, d_ff_3_q,
       multiplexer_1_out, multiplexer_2_out, multiplexer_3_out, multiplexer_4_out, multiplexer_5_out,
       multiplexer_6_out;

  Multiplexer multiplexer_1 (.sel(d_ff_1_q), .in_0(Store1_m_0), .in_1(Load1_m_0), .out(multiplexer_1_out));
  Multiplexer multiplexer_2 (.sel(d_ff_1_q), .in_0(Store1_m_1), .in_1(Load1_m_1), .out(multiplexer_2_out));
  D_FF d_ff_1 (.D(and_1_out), .C(Clk), .Q(d_ff_1_q));  // open: nQ
  Multiplexer multiplexer_3 (.sel(d_ff_1_q), .in_0(Store1_m_2), .in_1(Load1_m_2), .out(multiplexer_3_out));
  and and_1 (and_1_out, _8_bit_memories_1_done, On_Off);
  _8_bit_register _8_bit_register_1 (
    .Clk(Clk), .i_7(_8_bit_memories_1_output_7), .i_6(_8_bit_memories_1_output_6),
    .i_5(_8_bit_memories_1_output_5), .i_4(_8_bit_memories_1_output_4), .i_3(_8_bit_memories_1_output_3),
    .i_2(_8_bit_memories_1_output_2), .i_1(_8_bit_memories_1_output_1), .i_0(_8_bit_memories_1_output_0),
    .Enable(d_ff_1_q), .o_7(_8_bit_register_1_o_7), .o_6(_8_bit_register_1_o_6), .o_5(_8_bit_register_1_o_5),
    .o_4(_8_bit_register_1_o_4), .o_3(_8_bit_register_1_o_3), .o_2(_8_bit_register_1_o_2),
    .o_1(_8_bit_register_1_o_1), .o_0(_8_bit_register_1_o_0));
  Multiplexer multiplexer_4 (.sel(d_ff_2_q), .in_0(Store2_m_0), .in_1(Load2_m_0), .out(multiplexer_4_out));
  _8_bit_memories _8_bit_memories_1 (
    .Clk(Clk), .InputBit_7(Store1_i_7), .InputBit_6(Store1_i_6), .InputBit_5(Store1_i_5),
    .InputBit_4(Store1_i_4), .InputBit_3(Store1_i_3), .InputBit_2(Store1_i_2), .InputBit_1(Store1_i_1),
    .InputBit_0(Store1_i_0), .SelMemory_2(multiplexer_3_out), .SelMemory_1(multiplexer_2_out),
    .SelMemory_0(multiplexer_1_out), .Read_Write(Store1_r_w), .On_Off(On_Off),
    .Output_7(_8_bit_memories_1_output_7), .Output_6(_8_bit_memories_1_output_6),
    .Output_5(_8_bit_memories_1_output_5), .Output_4(_8_bit_memories_1_output_4),
    .Output_3(_8_bit_memories_1_output_3), .Output_2(_8_bit_memories_1_output_2),
    .Output_1(_8_bit_memories_1_output_1), .Output_0(_8_bit_memories_1_output_0),
    .Done(_8_bit_memories_1_done));
  Multiplexer multiplexer_5 (.sel(d_ff_2_q), .in_0(Store2_m_1), .in_1(Load2_m_1), .out(multiplexer_5_out));
  D_FF d_ff_2 (.D(and_2_out), .C(Clk), .Q(d_ff_2_q));  // open: nQ
  Multiplexer multiplexer_6 (.sel(d_ff_2_q), .in_0(Store2_m_2), .in_1(Load2_m_2), .out(multiplexer_6_out));
  and and_2 (and_2_out, _8_bit_memories_2_done, On_Off);
  and and_3 (and_3_out, and_2_out, Substraction, and_1_out);
  _8_bit_register _8_bit_register_2 (
    .Clk(Clk), .i_7(_8_bit_memories_2_output_7), .i_6(_8_bit_memories_2_output_6),
    .i_5(_8_bit_memories_2_output_5), .i_4(_8_bit_memories_2_output_4), .i_3(_8_bit_memories_2_output_3),
    .i_2(_8_bit_memories_2_output_2), .i_1(_8_bit_memories_2_output_1), .i_0(_8_bit_memories_2_output_0),
    .Enable(d_ff_2_q), .o_7(_8_bit_register_2_o_7), .o_6(_8_bit_register_2_o_6), .o_5(_8_bit_register_2_o_5),
    .o_4(_8_bit_register_2_o_4), .o_3(_8_bit_register_2_o_3), .o_2(_8_bit_register_2_o_2),
    .o_1(_8_bit_register_2_o_1), .o_0(_8_bit_register_2_o_0));
  _8_bit_memories _8_bit_memories_2 (
    .Clk(Clk), .InputBit_7(Store2_i_7), .InputBit_6(Store2_i_6), .InputBit_5(Store2_i_5),
    .InputBit_4(Store2_i_4), .InputBit_3(Store2_i_3), .InputBit_2(Store2_i_2), .InputBit_1(Store2_i_1),
    .InputBit_0(Store2_i_0), .SelMemory_2(multiplexer_6_out), .SelMemory_1(multiplexer_5_out),
    .SelMemory_0(multiplexer_4_out), .Read_Write(Store2_r_w), .On_Off(On_Off),
    .Output_7(_8_bit_memories_2_output_7), .Output_6(_8_bit_memories_2_output_6),
    .Output_5(_8_bit_memories_2_output_5), .Output_4(_8_bit_memories_2_output_4),
    .Output_3(_8_bit_memories_2_output_3), .Output_2(_8_bit_memories_2_output_2),
    .Output_1(_8_bit_memories_2_output_1), .Output_0(_8_bit_memories_2_output_0),
    .Done(_8_bit_memories_2_done));
  alu alu_1 (
    .i_1_bit_7(_8_bit_register_2_o_7), .i_1_bit_6(_8_bit_register_2_o_6), .i_1_bit_5(_8_bit_register_2_o_5),
    .i_1_bit_4(_8_bit_register_2_o_4), .i_1_bit_3(_8_bit_register_2_o_3), .i_1_bit_2(_8_bit_register_2_o_2),
    .i_1_bit_1(_8_bit_register_2_o_1), .i_1_bit_0(_8_bit_register_2_o_0), .i_2_bit_7(_8_bit_register_1_o_7),
    .i_2_bit_6(_8_bit_register_1_o_6), .i_2_bit_5(_8_bit_register_1_o_5), .i_2_bit_4(_8_bit_register_1_o_4),
    .i_2_bit_3(_8_bit_register_1_o_3), .i_2_bit_2(_8_bit_register_1_o_2), .i_2_bit_1(_8_bit_register_1_o_1),
    .i_2_bit_0(_8_bit_register_1_o_0), .On_Off(and_3_out), .Clk(Clk), .Done(alu_1_done),
    .o_bit_7(alu_1_o_bit_7), .o_bit_6(alu_1_o_bit_6), .o_bit_5(alu_1_o_bit_5), .o_bit_4(alu_1_o_bit_4),
    .o_bit_3(alu_1_o_bit_3), .o_bit_2(alu_1_o_bit_2), .o_bit_1(alu_1_o_bit_1), .o_bit_0(alu_1_o_bit_0));
  D_FF d_ff_3 (.D(alu_1_done), .C(Clk), .Q(d_ff_3_q));  // open: nQ
  _8_bit_memories _8_bit_memories_3 (
    .Clk(Clk), .InputBit_7(alu_1_o_bit_7), .InputBit_6(alu_1_o_bit_6), .InputBit_5(alu_1_o_bit_5),
    .InputBit_4(alu_1_o_bit_4), .InputBit_3(alu_1_o_bit_3), .InputBit_2(alu_1_o_bit_2),
    .InputBit_1(alu_1_o_bit_1), .InputBit_0(alu_1_o_bit_0), .SelMemory_2(Store3_m_2),
    .SelMemory_1(Store3_m_1), .SelMemory_0(Store3_m_0), .Read_Write(Store3_r_w), .On_Off(d_ff_3_q),
    .Output_7(_8_bit_memories_3_output_7), .Output_6(_8_bit_memories_3_output_6),
    .Output_5(_8_bit_memories_3_output_5), .Output_4(_8_bit_memories_3_output_4),
    .Output_3(_8_bit_memories_3_output_3), .Output_2(_8_bit_memories_3_output_2),
    .Output_1(_8_bit_memories_3_output_1), .Output_0(_8_bit_memories_3_output_0),
    .Done(_8_bit_memories_3_done));
  LED led_1 (.in(_8_bit_memories_3_output_7));
  LED led_2 (.in(_8_bit_memories_3_output_6));
  LED led_3 (.in(_8_bit_memories_3_output_5));
  LED led_4 (.in(_8_bit_memories_3_output_4));
  LED led_5 (.in(_8_bit_memories_3_output_3));
  LED led_6 (.in(_8_bit_memories_3_output_2));
  LED led_7 (.in(_8_bit_memories_3_output_1));
  LED led_8 (.in(_8_bit_memories_3_output_0));
  LED led_9 (.in(_8_bit_memories_3_output_0));
  LED led_10 (.in(_8_bit_memories_3_done));

  // Notes on the sheet:
  //   Substraction Instruction
  //   Store1 Instruction
  //   Store2 Instruction
  //   Load1 Instruction
  //   Load2 Instruction
  //   Store3 Instruction
endmodule
