// Digital circuit store.dig as structural Verilog
module store (
  input  i_0,
  input  i_1,
  input  i_2,
  input  i_3,
  input  i_4,
  input  i_5,
  input  i_6,
  input  i_7,
  input  m_0,
  input  m_1,
  input  m_2,
  input  r_w,
  input  Clk,
  input  on_off
);

  wire _8_bit_memories_1_done, _8_bit_memories_1_output_0, _8_bit_memories_1_output_1,
       _8_bit_memories_1_output_2, _8_bit_memories_1_output_3, _8_bit_memories_1_output_4,
       _8_bit_memories_1_output_5, _8_bit_memories_1_output_6, _8_bit_memories_1_output_7, and_1_out;

  _8_bit_memories _8_bit_memories_1 (
    .Clk(Clk), .InputBit_7(i_7), .InputBit_6(i_6), .InputBit_5(i_5), .InputBit_4(i_4), .InputBit_3(i_3),
    .InputBit_2(i_2), .InputBit_1(i_1), .InputBit_0(i_0), .SelMemory_2(m_2), .SelMemory_1(m_1),
    .SelMemory_0(m_0), .Read_Write(r_w), .On_Off(on_off), .Output_7(_8_bit_memories_1_output_7),
    .Output_6(_8_bit_memories_1_output_6), .Output_5(_8_bit_memories_1_output_5),
    .Output_4(_8_bit_memories_1_output_4), .Output_3(_8_bit_memories_1_output_3),
    .Output_2(_8_bit_memories_1_output_2), .Output_1(_8_bit_memories_1_output_1),
    .Output_0(_8_bit_memories_1_output_0), .Done(_8_bit_memories_1_done));
  and and_1 (and_1_out, _8_bit_memories_1_done, Clk);
  LED o_7 (.in(_8_bit_memories_1_output_7));
  LED o_6 (.in(_8_bit_memories_1_output_6));
  LED o_5 (.in(_8_bit_memories_1_output_5));
  LED o_4 (.in(_8_bit_memories_1_output_4));
  LED o_3 (.in(_8_bit_memories_1_output_3));
  LED o_2 (.in(_8_bit_memories_1_output_2));
  LED o_1 (.in(_8_bit_memories_1_output_1));
  LED o_0 (.in(_8_bit_memories_1_output_0));
  LED Done (.in(and_1_out));
  LED led_1 (.in(Clk));

  // Notes on the sheet:
  //   Input
endmodule
